# Fritzing sketch wifi_sensor (saved by Fritzing 0.9.3b)
circuit board: 6.88566cm x 5.36311cm
breadboards: 1

parts:
  U1 = Sharp PC817 [package=THT]
  LED1 = LED - 5mm [color="Red (633nm)" package="5 mm [THT]"]
  J1 = Screw terminal - 2 pins [package=THT]
  J2 = Screw terminal - 2 pins [package=THT]
  J3 = Screw terminal - 2 pins [package=THT]
  MCU = Arduino Uno (Rev3)
  Pad1 = Pad [width=2.8377057356608617 height=3.8258354114713216 connect=center]
  +V = Pad [width=3.775703345425232 height=3.061786913878811 connect=center]
  -V = Pad [width=3.775703345425232 height=3.061786913878811 connect=center]
  R2 = Resistor [tolerance=±5% resistance=10k package="2512 [SMD]"]
  R5 = Resistor [tolerance=±5% resistance=1k package="2512 [SMD]"]
  R3 = Resistor [tolerance=±5% resistance=1k package="2512 [SMD]"]
  J5 = Screw terminal - 2 pins [package=THT]
  Pad = Pad [width=3.4928461154153125 height=4.414765255221142 connect=center]  # not connected
  Pad2 = Pad [width=3.4928461154153125 height=4.414765255221142 connect=center]  # not connected
  Pad3 = Pad [width=3.4928461154153125 height=4.414765255221142 connect=center]  # not connected
  Pad4 = Pad [width=3.4928461154153125 height=4.414765255221142 connect=center]  # not connected
  Pad5 = Pad [width=3.4928461154153125 height=4.414765255221142 connect=center]  # not connected
  Pad6 = Pad [width=3.4928461154153125 height=4.414765255221142 connect=center]  # not connected
  R4 = Resistor [tolerance=±5% resistance=1k package="2512 [SMD]"]
  Pad7 = Pad [width=3.4928461154153125 height=4.414765255221142 connect=center]  # not connected
  Pad8 = Pad [width=3.4928461154153125 height=4.414765255221142 connect=center]  # not connected
  R1 = Resistor [tolerance=±5% resistance=1k package="2512 [SMD]"]
  U2 = Sharp PC817 [package=THT]
  LED2 = LED - 5mm [color="Red (633nm)" package="5 mm [THT]"]
  J4 = Screw terminal - 2 pins [package=THT]
  Pad9 = Pad [width=3.4928461154153125 height=4.414765255221142 connect=center]
  Pad10 = Pad [width=3.4928461154153125 height=4.414765255221142 connect=center]  # not connected
  R6 = Resistor [tolerance=±5% resistance=1k package="2512 [SMD]"]
  J6 = Screw terminal - 2 pins [package=THT]
  J7 = Screw terminal - 2 pins [package=THT]
  Pad11 = Pad [width=3.4928461154153125 height=4.414765255221142 connect=center]
  Pad12 = Pad [width=3.4928461154153125 height=4.414765255221142 connect=center]
  Pad13 = Pad [width=3.4928461154153125 height=4.414765255221142 connect=center]  # not connected
  Pad14 = Pad [width=3.4928461154153125 height=4.414765255221142 connect=center]  # not connected

nets:
  N1: U1.Pin_1, J1.pin2, J3.pin1, MCU.VIN, +V.pad, J5.pin2, U2.Pin_1
  N2: U1.Pin_2, R5.Pin_1
  N3: U1.Pin_4, MCU.D13/SCK, R2.Pin_0, R3.Pin_0
  N4: U1.Pin_3, LED1.anode, J1.pin1, J2.pin2, MCU.GND, Pad1.pad, -V.pad, J5.pin1, U2.Pin_3, LED2.anode, J7.pin1
  N5: LED1.cathode, R3.Pin_1
  N6: J2.pin1, R4.Pin_0
  N7: J3.pin2, R5.Pin_0, R6.Pin_1
  N8: MCU.A0, J4.pin1
  N9: MCU.D0/RX, J6.pin2, Pad12.pad
  N10: MCU.D1/TX, J6.pin1, Pad11.pad
  N11: MCU.D2, R1.Pin_0, U2.Pin_4, LED2.cathode
  N12: MCU.5V, R2.Pin_1, R1.Pin_1, J7.pin2
  N13: R4.Pin_1, U2.Pin_2
  N14: J4.pin2, Pad9.pad, R6.Pin_0

notes:
  +v
  -v
  npn
  General Imaging
  PR-Cmn v2
  pnp
  A0
  AL
  TX
  RX
  -V
  Vn
